// Logisim project cputest.circ as structural Verilog: 4 circuits, main circuit main
module main (
  input  [3:0] in_1,
  input  [7:0] in_2,
  input  [7:0] in_3,
  output [7:0] out_4
);

  ALU alu_1 (.\选择端 (in_1), .in_2(in_2), .in_3(in_3), .out_4(out_4));
endmodule

module ALU (
  input  [3:0] \选择端 ,
  input  [7:0] in_2,
  input  [7:0] in_3,
  output [7:0] out_4
);

  wire [7:0] AU_sum, LU_out_4;

  AU AU (.CRT(\选择端 [0]), .A(in_2), .B(in_2), .sum(AU_sum));
  LU LU (.in_1(\选择端 [0]), .A(in_2), .B(in_2), .out_4(LU_out_4));
  Multiplexer #(.width(8), .enable("false")) multiplexer_1 (.in0(AU_sum), .in1(LU_out_4), .out(out_4), .sel(\选择端 [1]));

  assign in_3 = in_2;
endmodule

module AU (
  input  CRT,
  input  [7:0] A,
  input  [7:0] B,
  output [7:0] sum
);

  wire [7:0] adder_1_out, multiplexer_1_out, not_1_out;

  assign not_1_out = ~B;  // NOT_Gate not_1, 8 bits wide
  Multiplexer #(.width(8), .enable("false")) multiplexer_1 (
    .in0(B), .in1(adder_1_out), .out(multiplexer_1_out), .sel(CRT));
  Adder adder_1 (.a(not_1_out), .b(8'h1), .out(adder_1_out));  // open: cin, cout
  Adder adder_2 (.a(A), .b(multiplexer_1_out), .out(sum));  // open: cin, cout
endmodule

module LU (
  input  in_1,
  input  [7:0] A,
  input  [7:0] B,
  output [7:0] out_4
);

  wire [7:0] and_1_out, or_1_out;

  assign and_1_out = A & B;  // AND_Gate and_1, 8 bits wide
  assign or_1_out = A | B;  // OR_Gate or_1, 8 bits wide
  Multiplexer #(.width(8), .enable("false")) multiplexer_1 (.in0(and_1_out), .in1(or_1_out), .out(out_4), .sel(in_1));
endmodule
